# Fritzing sketch esp32-laser-security-project (saved by Fritzing 1.0.1rc)

parts:
  BAT1 = 18650 battery holder [package=battery-18650-kit]
  M1 = ESP32-S3-DevKitC-1-N8R8-v1 [part_number=ESP32-S3-DevKitC-1-N8R8-v1]
  M2 = MT3608 Module
  TP1 = TP4056 [chip_label=TP4056 package="DIP (Dual Inline) [THT]"]
  J3 = Generic female header - 1 pins [form="♀ (female)" package=THT]
  J4 = Piezo Speaker
  LED1 = DUO LED RG [package="5 mm [THT]"]

nets:
  N1: BAT1.+, TP1.pin5
  N2: BAT1.-, TP1.pin4
  N3: M1.pin_1, M1.pin_2, J3.pin_7
  N4: M1.pin_4, J3.pin1
  N5: M1.pin_5, J3.pin_3
  N6: M1.pin_11, J3.pin_2
  N7: M1.pin_21, M2.pin3
  N8: M1.pin_24, M1.pin_44, M2.pin4, J3.pin_6
  N9: M1.pin_25, J3.pin_4
  N10: M1.pin_27, J3.pin_5
  N11: M2.pin1, TP1.pin6
  N12: M2.pin2, TP1.pin3
  N13: J3.pin_8, LED1.red_anode
  N14: J3.pin_9, LED1.common_cathode
  N15: J3.pin_10, LED1.green_anode
  N16: J3.pin_11, J4.pin1
  N17: J3.pin_12, J4.pin2

custom parts:
  18650 battery holder: 18650 Battery
  ESP32-S3-DevKitC-1-N8R8-v1: ESP32-S3-DevKitC-1-N8R8-v1 This module is 44pins long (2x22) and 11 pins width.
  MT3608 Module: MT3608 Boost Converter Module Links: Aerosemi MT3608 2A Step Up Converter datasheet
  TP4056: A DIP stand-in part for whatever IC you want. With 6 pins on a 300mil dual inline package (DIP) footprint.
  Generic female header - 1 pins: Generic female header
