# Fritzing sketch laser-power-supply (saved by Fritzing 1.0.1rc)

parts:
  BAT1 = 18650 battery holder [package=battery-18650-kit]
  J1 = Generic female header - 1 pins [form="♀ (female)" package=THT]
  U5 = SWITCH-SPST-2 [package=switch-spst-vertical]

nets:
  N1: BAT1.+, J1.pin1
  N2: BAT1.-, U5.O
  N3: J1.pin_2, U5.P

custom parts:
  18650 battery holder: 18650 Battery
  Generic female header - 1 pins: Generic female header
